# Fritzing sketch Untitled Sketch 5 (saved by Fritzing 0.9.3b)

parts:
  Part1 = Arduino Uno (Rev3)
  hc-sr2 = hc-sr04
  LED1 = LEDs [package=led10mm]
  LED2 = LEDs [package=led10mm]

nets:
  N1: Part1.D11_PWM/MOSI, hc-sr2.Echo
  N2: Part1.D13/SCK, hc-sr2.Trig
  GND: Part1.GND, hc-sr2.GND, LED1.C
  N3: Part1.D2, LED1.A
  N4: Part1.D4, LED2.A
  5V: Part1.5V, hc-sr2.VCC
