# Fritzing sketch Untitled Sketch 6 (saved by Fritzing 0.9.3b)
breadboards: 1

parts:
  Part2 = Arduino Uno (Rev3)
  hc-sr3 = hc-sr04
  LED1 = LEDs [package=led10mm]
  LED2 = LEDs [package=led10mm]

nets:
  N1: Part2.D9_PWM, hc-sr3.Trig
  N2: Part2.D10_PWM/SS, hc-sr3.Echo
  N3: Part2.D2, LED1.A
  N4: Part2.D4, LED2.A
  5V: Part2.5V, hc-sr3.VCC
  GND: Part2.GND, hc-sr3.GND, LED1.C, LED2.C
